# Fritzing sketch kapıesp32 (saved by Fritzing 0.9.4)

parts:
  MH-ET_LIVE_ESP32_DEVKIT1 = MH-ET LIVE ESP32 DEVKIT 38 pins
  J1 = Basic Servo
  LED1 = smd LED [color="Red (633nm)" package="1206 [SMD]"]  # not connected
  LED2 = smd LED [color="Green (570nm)" package="1206 [SMD]"]  # not connected
  HC-SR04_Sensor_1 = HC-SR04 Ultrasonic Distance Sensor
  Parça1 = RFID-RC522-v3
  LCM1602_IIC1 = LCM1602 IIC [part_number="LCM1602 IIC" chip_label="LCM1602 IIC" package="DIP (Dual Inline) [THT]"]
  LCD1 = LCD screen
  R1 = Resistor [tolerance=±5% resistance=220 package=THT]  # not connected
  R2 = Resistor [tolerance=±5% resistance=220 package=THT]  # not connected

nets:
  N1: MH-ET_LIVE_ESP32_DEVKIT1.IO26, J1.pulse
  N2: MH-ET_LIVE_ESP32_DEVKIT1.IO12, HC-SR04_Sensor_1.ECHO
  N3: MH-ET_LIVE_ESP32_DEVKIT1.IO13, HC-SR04_Sensor_1.TRIG
  GND: MH-ET_LIVE_ESP32_DEVKIT1.CMD, J1.gnd, LCM1602_IIC1.GND
  VCC: MH-ET_LIVE_ESP32_DEVKIT1.5V, J1.vcc, HC-SR04_Sensor_1.VCC, LCM1602_IIC1.VCC
  GND_2: MH-ET_LIVE_ESP32_DEVKIT1.GND, HC-SR04_Sensor_1.GND
  N4: MH-ET_LIVE_ESP32_DEVKIT1.IO23, Parça1.MOSI
  N5: MH-ET_LIVE_ESP32_DEVKIT1.IO22, LCM1602_IIC1.SCL
  N6: MH-ET_LIVE_ESP32_DEVKIT1.IO21, LCM1602_IIC1.SDA
  N7: MH-ET_LIVE_ESP32_DEVKIT1.IO19, Parça1.MISO
  N8: MH-ET_LIVE_ESP32_DEVKIT1.IO18, Parça1.SCK
  N9: MH-ET_LIVE_ESP32_DEVKIT1.IO5, Parça1.SDA
  VSS: LCM1602_IIC1.VSS, LCD1.VSS
  VDD: LCM1602_IIC1.VDD, LCD1.VDD
  N10: LCM1602_IIC1.V0, LCD1.V0
  N11: LCM1602_IIC1.RS, LCD1.RS
  N12: LCM1602_IIC1.RW, LCD1.R/W
  N13: LCM1602_IIC1.E, LCD1.E
  N14: LCM1602_IIC1.D0, LCD1.DB0
  N15: LCM1602_IIC1.D1, LCD1.DB1
  N16: LCM1602_IIC1.D2, LCD1.DB2
  N17: LCM1602_IIC1.D3, LCD1.DB3
  N18: LCM1602_IIC1.D4, LCD1.DB4
  N19: LCM1602_IIC1.D5, LCD1.DB5
  N20: LCM1602_IIC1.D6, LCD1.DB6
  N21: LCM1602_IIC1.D7, LCD1.DB7
  N22: LCM1602_IIC1.A, LCD1.LED+
  N23: LCM1602_IIC1.K, LCD1.LED-

custom parts:
  MH-ET LIVE ESP32 DEVKIT 38 pins: http://mh.nodebb.com/topic/2/mh-et-live-esp32-devkit
  RFID-RC522-v3: A simple China made RFID-RC522 Reader (6x4 cm); do check the pin labels, as this is a MFRC522 based clone.
  LCM1602 IIC: I2C-Module to use a 1602 or 2004 LCD on with the wire.h libory Serial LCD Modul
